# Fritzing sketch Pi.fritz (saved by Fritzing 0.9.0b)

parts:
  Raspberry_Pi_B_rev1 = Raspberry Pi B rev1
  S1 = Pushbutton [package="[SMD]"]

nets:
  N1: Raspberry_Pi_B_rev1.GPIO_0, S1.Pin_3, S1.Pin_4
  N2: Raspberry_Pi_B_rev1.GND, S1.Pin_1, S1.Pin_2
